// Logisim project final number guesser!!!.circ as structural Verilog: 19 circuits, main circuit main
module main (
  output [3:0] out_1
);

  wire _0_out, _1_out, _2_out, _3_out, _4_out, _5_out, _6_out, _7_out, _8_out, _9_out, a_out, b_out, C_out,
       clear_out, comparator_1_eq, d_out, decoder_1_e, decoder_1_f, decoder_1_g, decoder_1_h, decoder_1_i,
       decoder_1_j, decoder_1_k, E_out, F_out, not_1_out, one_1_1_out_18, one_1_1_out_19, one_1_1_out_20,
       one_1_1_out_21, one_1_1_out_22, one_1_1_out_23, one_1_1_out_24;
  wire [3:0] one_1_1_out_25, undriven;

  Button _1 (.out(_1_out));
  Button _4 (.out(_4_out));
  Button _7 (.out(_7_out));
  Button a (.out(a_out));
  Button _3 (.out(_3_out));
  Button _2 (.out(_2_out));
  Button _5 (.out(_5_out));
  Button _6 (.out(_6_out));
  Button _9 (.out(_9_out));
  Button _8 (.out(_8_out));
  Button _0 (.out(_0_out));
  Button b (.out(b_out));
  Button C (.out(C_out));
  Button d (.out(d_out));
  Button E (.out(E_out));
  Button F (.out(F_out));
  Button clear (.out(clear_out));
  one_1 one_1_1 (
    .in_1(_1_out), .in_2(_2_out), .in_3(_3_out), .in_4(_4_out), .in_5(_5_out), .in_6(_6_out), .in_7(_7_out),
    .in_8(_8_out), .in_9(_9_out), .in_10(_0_out), .in_11(a_out), .in_12(b_out), .in_13(C_out), .in_14(d_out),
    .in_15(E_out), .in_16(F_out), .out_22(one_1_1_out_22), .out_23(one_1_1_out_23), .out_24(one_1_1_out_24),
    .in_17(clear_out), .out_18(one_1_1_out_18), .out_19(one_1_1_out_19), .out_20(one_1_1_out_20),
    .out_21(one_1_1_out_21), .out_25(one_1_1_out_25));
  Random #(.width(4)) random_1 (.clk(clear_out), .out(out_1));  // open: next, clr
  decoder decoder_1 (
    .A(undriven[0]), .D(undriven[1]), .C(undriven[2]), .B(undriven[3]), .e(decoder_1_e), .f(decoder_1_f),
    .g(decoder_1_g), .h(decoder_1_h), .i(decoder_1_i), .j(decoder_1_j), .k(decoder_1_k));
  Comparator #(.width(4)) comparator_1 (.a(one_1_1_out_25), .b(out_1), .eq(comparator_1_eq));  // open: gt, lt
  _7_Segment_Display u_7_segment_display_1 (
    .g(decoder_1_k), .f(decoder_1_j), .a(decoder_1_e), .b(decoder_1_f), .e(decoder_1_i), .d(decoder_1_h),
    .c(decoder_1_g));  // open: dp
  _7_Segment_Display u_7_segment_display_2 (
    .g(one_1_1_out_18), .f(one_1_1_out_19), .a(one_1_1_out_20), .b(one_1_1_out_21), .e(one_1_1_out_22),
    .d(one_1_1_out_23), .c(one_1_1_out_24));  // open: dp
  not not_1 (not_1_out, comparator_1_eq);
  LED led_1 (.in(not_1_out));
  LED led_2 (.in(comparator_1_eq));
endmodule

module decoder (
  input  A,
  input  D,
  input  C,
  input  B,
  output e,
  output f,
  output g,
  output h,
  output i,
  output j,
  output k
);

  wire and_1_out, and_2_out, and_3_out, and_4_out, and_5_out, and_6_out, and_7_out, and_8_out, and_9_out,
       and_10_out, and_11_out, and_12_out, and_13_out, and_14_out, and_15_out, and_16_out, and_17_out,
       and_18_out, and_19_out, and_20_out, and_21_out, and_22_out, and_23_out, and_24_out, and_25_out,
       and_26_out, and_27_out, and_28_out, and_29_out, and_30_out, and_31_out, and_32_out, and_33_out,
       and_34_out, and_35_out, not_1_out, not_2_out, not_3_out, not_4_out, not_5_out, not_6_out, not_7_out,
       not_8_out, not_9_out, not_10_out, not_11_out, not_12_out, not_13_out, not_14_out, not_15_out,
       not_16_out, not_17_out, not_18_out, not_19_out, not_20_out, not_21_out, not_22_out, not_23_out,
       not_24_out, not_25_out, not_26_out, not_27_out, not_28_out, not_29_out, not_30_out, not_31_out,
       not_32_out, not_33_out, not_34_out, not_35_out, not_36_out, not_37_out, not_38_out, not_39_out,
       not_40_out, not_41_out, not_42_out;

  not not_1 (not_1_out, A);
  and and_1 (and_1_out, not_1_out, not_2_out);
  not not_2 (not_2_out, C);
  not not_3 (not_3_out, A);
  and and_2 (and_2_out, not_3_out, B);
  not not_4 (not_4_out, D);
  and and_3 (and_3_out, not_4_out, not_5_out, B);
  not not_5 (not_5_out, C);
  and and_4 (and_4_out, D, not_6_out);
  not not_6 (not_6_out, B);
  and and_5 (and_5_out, D, C);
  and and_6 (and_6_out, A, C, not_7_out);
  not not_7 (not_7_out, B);
  not not_8 (not_8_out, A);
  not not_9 (not_9_out, D);
  and and_7 (and_7_out, not_8_out, not_9_out, not_10_out);
  not not_10 (not_10_out, B);
  not not_11 (not_11_out, A);
  and and_8 (and_8_out, not_11_out, not_12_out);
  not not_12 (not_12_out, C);
  not not_13 (not_13_out, D);
  and and_9 (and_9_out, not_13_out, not_14_out);
  not not_14 (not_14_out, C);
  and and_10 (and_10_out, A, not_15_out, B);
  not not_15 (not_15_out, D);
  and and_11 (and_11_out, A, D, not_16_out);
  not not_16 (not_16_out, B);
  not not_17 (not_17_out, D);
  and and_12 (and_12_out, not_17_out, not_18_out);
  not not_18 (not_18_out, C);
  not not_19 (not_19_out, C);
  and and_13 (and_13_out, not_19_out, B);
  and and_14 (and_14_out, C, not_20_out);
  not not_20 (not_20_out, B);
  and and_15 (and_15_out, A, not_21_out);
  not not_21 (not_21_out, D);
  and and_16 (and_16_out, A, not_22_out);
  not not_22 (not_22_out, C);
  not not_23 (not_23_out, A);
  and and_17 (and_17_out, not_23_out, not_24_out);
  not not_24 (not_24_out, C);
  not not_25 (not_25_out, D);
  and and_18 (and_18_out, not_25_out, B);
  not not_26 (not_26_out, A);
  and and_19 (and_19_out, not_26_out, D);
  and and_20 (and_20_out, D, not_27_out);
  not not_27 (not_27_out, C);
  not not_28 (not_28_out, D);
  and and_21 (and_21_out, A, not_28_out, C);
  not not_29 (not_29_out, A);
  and and_22 (and_22_out, not_29_out, not_30_out);
  not not_30 (not_30_out, C);
  and and_23 (and_23_out, C, B);
  not not_31 (not_31_out, A);
  and and_24 (and_24_out, not_31_out, D);
  and and_25 (and_25_out, D, B);
  not not_32 (not_32_out, A);
  and and_26 (and_26_out, not_32_out, not_33_out);
  not not_33 (not_33_out, D);
  not not_34 (not_34_out, A);
  and and_27 (and_27_out, not_34_out, C);
  not not_35 (not_35_out, D);
  and and_28 (and_28_out, not_35_out, C, not_36_out);
  not not_36 (not_36_out, B);
  not not_37 (not_37_out, C);
  and and_29 (and_29_out, A, not_37_out, B);
  and and_30 (and_30_out, A, D, B);
  not not_38 (not_38_out, C);
  and and_31 (and_31_out, not_38_out, B);
  not not_39 (not_39_out, D);
  and and_32 (and_32_out, not_39_out, C, not_40_out);
  not not_40 (not_40_out, B);
  not not_41 (not_41_out, A);
  and and_33 (and_33_out, not_41_out, D);
  and and_34 (and_34_out, D, not_42_out);
  not not_42 (not_42_out, C);
  and and_35 (and_35_out, A, B);
  or or_1 (f, and_7_out, and_8_out, and_9_out, and_10_out, and_11_out);
  or or_2 (g, and_12_out, and_13_out, and_14_out, and_15_out, and_16_out);
  or or_3 (h, and_17_out, and_18_out, and_19_out, and_20_out, and_21_out);
  or or_4 (i, and_22_out, and_23_out, and_24_out, and_25_out);
  or or_5 (j, and_26_out, and_27_out, and_28_out, and_29_out, and_30_out);
  or or_6 (k, and_31_out, and_32_out, and_33_out, and_34_out, and_35_out);
  or or_7 (e, and_1_out, and_2_out, and_3_out, and_4_out, and_5_out, and_6_out);
endmodule

module one (
  input  in_1,
  input  in_2,
  output out_3,
  output out_4,
  output out_5,
  output out_6
);

  wire j_k_ff_1_q;

  J_K_Flip_Flop j_k_ff_1 (.J(1'b1), .clk(in_1), .K(1'b1), .Q(j_k_ff_1_q), .reset(in_2));  // open: Qn, preset, en
  Multiplexer #(.width(4)) multiplexer_1 (
    .in1(4'b0001), .out({out_6, out_5, out_4, out_3}), .sel(1'b1), .en(j_k_ff_1_q));  // open: in0
endmodule

module one_1 (
  input  in_1,
  input  in_2,
  input  in_3,
  input  in_4,
  input  in_5,
  input  in_6,
  input  in_7,
  input  in_8,
  input  in_9,
  input  in_10,
  input  in_11,
  input  in_12,
  input  in_13,
  input  in_14,
  input  in_15,
  input  in_16,
  input  in_17,
  output out_18,
  output out_19,
  output out_20,
  output out_21,
  output out_22,
  output out_23,
  output out_24,
  output [3:0] out_25
);

  one one_1 (.in_1(in_1), .in_2(in_17), .out_3(out_25[0]), .out_4(out_25[1]), .out_5(out_25[2]), .out_6(out_25[3]));
  two two_1 (.in_1(in_2), .in_2(in_17), .out_3(out_25[0]), .out_4(out_25[1]), .out_5(out_25[2]), .out_6(out_25[3]));
  three three_1 (.in_1(in_3), .in_2(in_17), .out_3(out_25[0]), .out_4(out_25[1]), .out_5(out_25[2]), .out_6(out_25[3]));
  four four_1 (.in_1(in_4), .in_2(in_17), .out_3(out_25[0]), .out_4(out_25[1]), .out_5(out_25[2]), .out_6(out_25[3]));
  five five_1 (.in_1(in_5), .in_2(in_17), .out_3(out_25[0]), .out_4(out_25[1]), .out_5(out_25[2]), .out_6(out_25[3]));
  six six_1 (.in_1(in_6), .in_2(in_17), .out_3(out_25[0]), .out_4(out_25[1]), .out_5(out_25[2]), .out_6(out_25[3]));
  seven seven_1 (.in_1(in_7), .in_2(in_17), .out_3(out_25[0]), .out_4(out_25[1]), .out_5(out_25[2]), .out_6(out_25[3]));
  eight eight_1 (.in_1(in_8), .in_2(in_17), .out_3(out_25[0]), .out_4(out_25[1]), .out_5(out_25[2]), .out_6(out_25[3]));
  nine nine_1 (.in_1(in_9), .in_2(in_17), .out_3(out_25[0]), .out_4(out_25[1]), .out_5(out_25[2]), .out_6(out_25[3]));
  a a_1 (.in_1(in_11), .in_2(in_17), .out_3(out_25[0]), .out_4(out_25[1]), .out_5(out_25[2]), .out_6(out_25[3]));
  b b_1 (.in_1(in_12), .in_2(in_17), .out_3(out_25[0]), .out_4(out_25[1]), .out_5(out_25[2]), .out_6(out_25[3]));
  c c_1 (.in_1(in_13), .in_2(in_17), .out_3(out_25[0]), .out_4(out_25[1]), .out_5(out_25[2]), .out_6(out_25[3]));
  d d_1 (.in_1(in_14), .in_2(in_17), .out_3(out_25[0]), .out_4(out_25[1]), .out_5(out_25[2]), .out_6(out_25[3]));
  e e_1 (.in_1(in_15), .in_2(in_17), .out_3(out_25[0]), .out_4(out_25[1]), .out_5(out_25[2]), .out_6(out_25[3]));
  f f_1 (.in_1(in_16), .in_2(in_17), .out_3(out_25[0]), .out_4(out_25[1]), .out_5(out_25[2]), .out_6(out_25[3]));
  decoder decoder_1 (
    .A(out_25[0]), .D(out_25[1]), .C(out_25[2]), .B(out_25[3]), .e(out_20), .f(out_21), .g(out_24),
    .h(out_23), .i(out_22), .j(out_19), .k(out_18));
  zero zero_1 (.in_1(in_10), .in_2(in_17), .out_3(out_25[0]), .out_4(out_25[1]), .out_5(out_25[2]), .out_6(out_25[3]));
  _7_Segment_Display u_7_segment_display_1 ();  // open: g, f, a, b, e, d, c, dp
endmodule

module two (
  input  in_1,
  input  in_2,
  output out_3,
  output out_4,
  output out_5,
  output out_6
);

  wire j_k_ff_1_q;

  J_K_Flip_Flop j_k_ff_1 (.J(1'b1), .clk(in_1), .K(1'b1), .Q(j_k_ff_1_q), .reset(in_2));  // open: Qn, preset, en
  Multiplexer #(.width(4)) multiplexer_1 (
    .in1(4'b0010), .out({out_6, out_5, out_4, out_3}), .sel(1'b1), .en(j_k_ff_1_q));  // open: in0
endmodule

module three (
  input  in_1,
  input  in_2,
  output out_3,
  output out_4,
  output out_5,
  output out_6
);

  wire j_k_ff_1_q;

  J_K_Flip_Flop j_k_ff_1 (.J(1'b1), .clk(in_1), .K(1'b1), .Q(j_k_ff_1_q), .reset(in_2));  // open: Qn, preset, en
  Multiplexer #(.width(4)) multiplexer_1 (
    .in1(4'b0011), .out({out_6, out_5, out_4, out_3}), .sel(1'b1), .en(j_k_ff_1_q));  // open: in0
endmodule

module four (
  input  in_1,
  input  in_2,
  output out_3,
  output out_4,
  output out_5,
  output out_6
);

  wire j_k_ff_1_q;

  J_K_Flip_Flop j_k_ff_1 (.J(1'b1), .clk(in_1), .K(1'b1), .Q(j_k_ff_1_q), .reset(in_2));  // open: Qn, preset, en
  Multiplexer #(.width(4)) multiplexer_1 (
    .in1(4'b0100), .out({out_6, out_5, out_4, out_3}), .sel(1'b1), .en(j_k_ff_1_q));  // open: in0
endmodule

module five (
  input  in_1,
  input  in_2,
  output out_3,
  output out_4,
  output out_5,
  output out_6
);

  wire j_k_ff_1_q;

  J_K_Flip_Flop j_k_ff_1 (.J(1'b1), .clk(in_1), .K(1'b1), .Q(j_k_ff_1_q), .reset(in_2));  // open: Qn, preset, en
  Multiplexer #(.width(4)) multiplexer_1 (
    .in1(4'b0101), .out({out_6, out_5, out_4, out_3}), .sel(1'b1), .en(j_k_ff_1_q));  // open: in0
endmodule

module six (
  input  in_1,
  input  in_2,
  output out_3,
  output out_4,
  output out_5,
  output out_6
);

  wire j_k_ff_1_q;

  J_K_Flip_Flop j_k_ff_1 (.J(1'b1), .clk(in_1), .K(1'b1), .Q(j_k_ff_1_q), .reset(in_2));  // open: Qn, preset, en
  Multiplexer #(.width(4)) multiplexer_1 (
    .in1(4'b0110), .out({out_6, out_5, out_4, out_3}), .sel(1'b1), .en(j_k_ff_1_q));  // open: in0
endmodule

module seven (
  input  in_1,
  input  in_2,
  output out_3,
  output out_4,
  output out_5,
  output out_6
);

  wire j_k_ff_1_q;

  J_K_Flip_Flop j_k_ff_1 (.J(1'b1), .clk(in_1), .K(1'b1), .Q(j_k_ff_1_q), .reset(in_2));  // open: Qn, preset, en
  Multiplexer #(.width(4)) multiplexer_1 (
    .in1(4'b0111), .out({out_6, out_5, out_4, out_3}), .sel(1'b1), .en(j_k_ff_1_q));  // open: in0
endmodule

module eight (
  input  in_1,
  input  in_2,
  output out_3,
  output out_4,
  output out_5,
  output out_6
);

  wire j_k_ff_1_q;

  J_K_Flip_Flop j_k_ff_1 (.J(1'b1), .clk(in_1), .K(1'b1), .Q(j_k_ff_1_q), .reset(in_2));  // open: Qn, preset, en
  Multiplexer #(.width(4)) multiplexer_1 (
    .in1(4'b1000), .out({out_6, out_5, out_4, out_3}), .sel(1'b1), .en(j_k_ff_1_q));  // open: in0
endmodule

module nine (
  input  in_1,
  input  in_2,
  output out_3,
  output out_4,
  output out_5,
  output out_6
);

  wire j_k_ff_1_q;

  J_K_Flip_Flop j_k_ff_1 (.J(1'b1), .clk(in_1), .K(1'b1), .Q(j_k_ff_1_q), .reset(in_2));  // open: Qn, preset, en
  Multiplexer #(.width(4)) multiplexer_1 (
    .in1(4'b1001), .out({out_6, out_5, out_4, out_3}), .sel(1'b1), .en(j_k_ff_1_q));  // open: in0
endmodule

module zero (
  input  in_1,
  input  in_2,
  output out_3,
  output out_4,
  output out_5,
  output out_6
);

  wire j_k_ff_1_q;

  J_K_Flip_Flop j_k_ff_1 (.J(1'b1), .clk(in_1), .K(1'b1), .Q(j_k_ff_1_q), .reset(in_2));  // open: Qn, preset, en
  Multiplexer #(.width(4)) multiplexer_1 (
    .in1(4'b0000), .out({out_6, out_5, out_4, out_3}), .sel(1'b1), .en(j_k_ff_1_q));  // open: in0
endmodule

module a (
  input  in_1,
  input  in_2,
  output out_3,
  output out_4,
  output out_5,
  output out_6
);

  wire j_k_ff_1_q;

  J_K_Flip_Flop j_k_ff_1 (.J(1'b1), .clk(in_1), .K(1'b1), .Q(j_k_ff_1_q), .reset(in_2));  // open: Qn, preset, en
  Multiplexer #(.width(4)) multiplexer_1 (
    .in1(4'b1010), .out({out_6, out_5, out_4, out_3}), .sel(1'b1), .en(j_k_ff_1_q));  // open: in0
endmodule

module b (
  input  in_1,
  input  in_2,
  output out_3,
  output out_4,
  output out_5,
  output out_6
);

  wire j_k_ff_1_q;

  J_K_Flip_Flop j_k_ff_1 (.J(1'b1), .clk(in_1), .K(1'b1), .Q(j_k_ff_1_q), .reset(in_2));  // open: Qn, preset, en
  Multiplexer #(.width(4)) multiplexer_1 (
    .in1(4'b1011), .out({out_6, out_5, out_4, out_3}), .sel(1'b1), .en(j_k_ff_1_q));  // open: in0
endmodule

module c (
  input  in_1,
  input  in_2,
  output out_3,
  output out_4,
  output out_5,
  output out_6
);

  wire j_k_ff_1_q;

  J_K_Flip_Flop j_k_ff_1 (.J(1'b1), .clk(in_1), .K(1'b1), .Q(j_k_ff_1_q), .reset(in_2));  // open: Qn, preset, en
  Multiplexer #(.width(4)) multiplexer_1 (
    .in1(4'b1100), .out({out_6, out_5, out_4, out_3}), .sel(1'b1), .en(j_k_ff_1_q));  // open: in0
endmodule

module d (
  input  in_1,
  input  in_2,
  output out_3,
  output out_4,
  output out_5,
  output out_6
);

  wire j_k_ff_1_q;

  J_K_Flip_Flop j_k_ff_1 (.J(1'b1), .clk(in_1), .K(1'b1), .Q(j_k_ff_1_q), .reset(in_2));  // open: Qn, preset, en
  Multiplexer #(.width(4)) multiplexer_1 (
    .in1(4'b1101), .out({out_6, out_5, out_4, out_3}), .sel(1'b1), .en(j_k_ff_1_q));  // open: in0
endmodule

module e (
  input  in_1,
  input  in_2,
  output out_3,
  output out_4,
  output out_5,
  output out_6
);

  wire j_k_ff_1_q;

  J_K_Flip_Flop j_k_ff_1 (.J(1'b1), .clk(in_1), .K(1'b1), .Q(j_k_ff_1_q), .reset(in_2));  // open: Qn, preset, en
  Multiplexer #(.width(4)) multiplexer_1 (
    .in1(4'b1110), .out({out_6, out_5, out_4, out_3}), .sel(1'b1), .en(j_k_ff_1_q));  // open: in0
endmodule

module f (
  input  in_1,
  input  in_2,
  output out_3,
  output out_4,
  output out_5,
  output out_6
);

  wire j_k_ff_1_q;

  J_K_Flip_Flop j_k_ff_1 (.J(1'b1), .clk(in_1), .K(1'b1), .Q(j_k_ff_1_q), .reset(in_2));  // open: Qn, preset, en
  Multiplexer #(.width(4)) multiplexer_1 (
    .in1(4'b1111), .out({out_6, out_5, out_4, out_3}), .sel(1'b1), .en(j_k_ff_1_q));  // open: in0
endmodule
